// Logisim project BeEight.circ as structural Verilog: 3 circuits, main circuit main
module main (
  input  in_1,
  input  D0,
  input  RESET,
  input  D1,
  input  HLT,
  input  D2,
  input  RES,
  input  D3,
  output [11:0] Address
);

  wire adder_2_cout, ALUD0, ALUD1, ALUD2, ALUD3, ALUD4, ALUD5, ALUD6, ALUD7, and_1_out, and_2_out, and_3_out,
       and_4_out, and_5_out, and_6_out, and_8_out, and_9_out, and_10_out, and_14_out, and_15_out, Carry, CLK,
       CLKIN, ConditionalFlag, ConditionalResult, controlled_buffer_11_out, controlled_buffer_14_out,
       controlled_buffer_15_out, controlled_buffer_16_out, controlled_buffer_17_out,
       controlled_buffer_18_out, controlled_buffer_19_out, controlled_buffer_20_out, Equal, GreaterThan, ia,
       ialu, im, inone, ipb, ipc, ipcs, isb, LessThan, n74138_1_pin4, n74138_1_pin5, n74138_1_pin6,
       n74138_2_pin4, n74138_2_pin5, n74138_2_pin6, n74138_3_pin4, n74138_3_pin5, n74138_3_pin6,
       n74138_3_pin7, n74138_3_pin9, n74138_3_pin10, n74138_3_pin11, n74138_3_pin12, n74138_3_pin13,
       n74138_3_pin14, n74138_3_pin15, n74161_1_pin7, n74161_1_pin10, n74161_1_pin15, n74161_2_pin10,
       n74161_2_pin15, n74161_3_pin10, n74161_4_pin1, n74161_4_pin2, n74161_4_pin7, n74161_4_pin9,
       n74161_4_pin10, nand_1_out, nand_3_out, nand_4_out, nor_1_out, not_1_out, not_2_out, not_3_out,
       not_4_out, not_5_out, not_7_out, not_8_out, not_9_out, not_10_out, not_11_out, not_12_out, not_13_out,
       not_14_out, not_15_out, not_16_out, not_17_out, not_18_out, not_19_out, not_20_out, not_23_out,
       not_24_out, not_25_out, not_26_out, not_27_out, not_28_out, not_29_out, not_31_out, not_32_out,
       not_33_out, not_34_out, not_35_out, not_36_out, not_37_out, not_38_out, not_39_out, not_40_out,
       not_41_out, nxt, oa, oalu, om, onone, opb, opc, opcs, or_1_out, or_2_out, or_3_out, osb,
       pull_resistor_2_node, pull_resistor_3_node, pull_resistor_11_node, RESET_t, s_r_ff_1_qn, special, ucf;
  wire [3:0] Condition, DatabusUpper, Instruction, InstructionCounter, pull_resistor_1_node;
  wire [6:0] rom_1_data;
  wire [7:0] Accumulator, Accumulator_q, adder_1_out, adder_2_out, ALU, ALUBuffer_q, Databus, nand_2_out,
       not_30_out, PrimaryBuffer, ProgramCounterStorageLower_q, ProgramCounterStorageUpper_q,
       SecondaryBuffer, SecondaryBuffer_q;
  wire [7:4] controlled_buffer_3_out;
  wire [11:0] StoredAddress;

  Pull_Resistor pull_resistor_1 (.node(pull_resistor_1_node));
  Hex_Digit_Display #(.decimalPoint("false")) hex_digit_display_1 (.value(Address[11:8]));
  Hex_Digit_Display #(.decimalPoint("false")) hex_digit_display_2 (.value(Instruction));
  Hex_Digit_Display #(.decimalPoint("false")) hex_digit_display_3 (.value(InstructionCounter));
  Hex_Digit_Display #(.decimalPoint("false")) hex_digit_display_4 (.value(Address[7:4]));
  Hex_Digit_Display #(.decimalPoint("false")) hex_digit_display_5 (.value(Address[3:0]));
  Hex_Digit_Display #(.decimalPoint("false")) hex_digit_display_6 (.value(DatabusUpper));
  Hex_Digit_Display #(.decimalPoint("false")) hex_digit_display_7 (.value(Databus[7:4]));
  Register ProgramCounterStorageLower (
    .D(Databus), .en(not_1_out), .clk(CLK), .Q(ProgramCounterStorageLower_q));  // open: clr
  not not_1 (not_1_out, ipcs);
  Register ProgramCounterStorageUpper (
    .D({pull_resistor_1_node, DatabusUpper}), .en(not_2_out), .clk(CLK), .Q(ProgramCounterStorageUpper_q));  // open: clr
  not not_2 (not_2_out, ipcs);
  Hex_Digit_Display #(.decimalPoint("false")) hex_digit_display_8 (.value(Accumulator[7:4]));
  Hex_Digit_Display #(.decimalPoint("false")) hex_digit_display_9 (.value(Accumulator[3:0]));
  Hex_Digit_Display #(.decimalPoint("false")) hex_digit_display_10 (.value(Databus[3:0]));
  not not_3 (not_3_out, im);
  not not_4 (not_4_out, om);
  not not_5 (not_5_out, opcs);
  Hex_Digit_Display #(.decimalPoint("false")) hex_digit_display_11 (.value(ALU[7:4]));
  Hex_Digit_Display #(.decimalPoint("false")) hex_digit_display_12 (.value(PrimaryBuffer[7:4]));
  Hex_Digit_Display #(.decimalPoint("false")) hex_digit_display_13 (.value(PrimaryBuffer[3:0]));
  not not_6 (RESET_t, RESET);
  Clock u_CLK (.out(CLKIN));
  RAM #(.addrWidth(12), .databus("bidir"), .trigger("high"), .\type ("nonvolatile")) ram_1 (
    .addr(Address), .we(not_3_out), .oe(not_4_out), .data(Databus));
  assign Databus = and_1_out ? ProgramCounterStorageLower_q : 8'bz;  // Controlled_Buffer controlled_buffer_1
  and and_1 (and_1_out, not_5_out, not_7_out);
  not not_7 (not_7_out, special);
  assign DatabusUpper = not_8_out ? ProgramCounterStorageUpper_q[3:0] : 4'bz;  // Controlled_Buffer controlled_buffer_2
  not not_8 (not_8_out, opcs);
  LED led_1 (.in(onone));
  LED led_2 (.in(inone));
  Hex_Digit_Display #(.decimalPoint("false")) hex_digit_display_14 (.value(ALU[3:0]));
  Hex_Digit_Display #(.decimalPoint("false")) hex_digit_display_15 (.value(SecondaryBuffer[7:4]));
  Hex_Digit_Display #(.decimalPoint("false")) hex_digit_display_16 (.value(SecondaryBuffer[3:0]));
  not not_9 (not_9_out, osb);
  LED led_3 (.in(om));
  LED led_4 (.in(opb));
  LED led_5 (.in(im));
  LED led_6 (.in(ipb));
  Hex_Digit_Display #(.decimalPoint("false")) hex_digit_display_17 (.value(StoredAddress[11:8]));
  Hex_Digit_Display #(.decimalPoint("false")) hex_digit_display_18 (.value(StoredAddress[7:4]));
  not not_10 (not_10_out, and_2_out);
  and and_2 (and_2_out, not_9_out, Instruction[0], Instruction[1], Instruction[2]);
  and and_3 (and_3_out, and_2_out, ConditionalFlag);
  LED led_7 (.in(osb));
  LED led_8 (.in(oa));
  LED led_9 (.in(isb));
  LED led_10 (.in(ia));
  Hex_Digit_Display #(.decimalPoint("false")) hex_digit_display_19 (.value(StoredAddress[3:0]));
  or or_1 (or_1_out, not_10_out, and_3_out);
  not not_11 (not_11_out, ipc);
  LED led_11 (.in(oalu));
  LED led_12 (.in(opc));
  LED led_13 (.in(ialu));
  LED led_14 (.in(ipc));
  LED led_15 (.in(special));
  LED led_16 (.in(CLK));
  LED led_17 (.in(nxt));
  LED led_18 (.in(ConditionalFlag));
  LED RD (.in(om));
  LED WR (.in(im));
  and and_4 (and_4_out, CLK, or_1_out, not_11_out);
  LED led_19 (.in(opcs));
  LED led_20 (.in(ipcs));
  and and_5 (and_5_out, and_4_out, not_13_out);
  and and_6 (and_6_out, and_4_out, not_13_out);
  _74161 #(.ShowInternalStructure("true")) u_74161_1 (
    .pin2(and_4_out), .pin3(Databus[0]), .pin4(Databus[1]), .pin5(Databus[2]), .pin6(Databus[3]),
    .pin7(n74161_1_pin7), .pin15(n74161_1_pin15), .pin14(Address[0]), .pin13(Address[1]), .pin12(Address[2]),
    .pin11(Address[3]), .pin10(n74161_1_pin10), .pin9(special));  // open: pin1
  _74161 #(.ShowInternalStructure("true")) u_74161_2 (
    .pin2(and_5_out), .pin3(Databus[4]), .pin4(Databus[5]), .pin5(Databus[6]), .pin6(Databus[7]),
    .pin7(n74161_1_pin15), .pin15(n74161_2_pin15), .pin14(Address[4]), .pin13(Address[5]),
    .pin12(Address[6]), .pin11(Address[7]), .pin10(n74161_2_pin10), .pin9(special));  // open: pin1
  _74161 #(.ShowInternalStructure("true")) u_74161_3 (
    .pin2(and_6_out), .pin3(DatabusUpper[0]), .pin4(DatabusUpper[1]), .pin5(DatabusUpper[2]),
    .pin6(DatabusUpper[3]), .pin7(n74161_2_pin15), .pin14(Address[8]), .pin13(Address[9]),
    .pin12(Address[10]), .pin11(Address[11]), .pin10(n74161_3_pin10), .pin9(special));  // open: pin1, pin15
  not not_12 (not_12_out, special);
  assign controlled_buffer_3_out = special ? Instruction : 4'bz;  // Controlled_Buffer controlled_buffer_3
  S_R_Flip_Flop s_r_ff_1 (.reset(RES), .Qn(s_r_ff_1_qn), .preset(HLT));  // open: S, R, clk, Q
  not not_13 (not_13_out, special);
  assign controlled_buffer_3_out = not_12_out ? Databus[7:4] : 4'bz;  // Controlled_Buffer controlled_buffer_4
  assign DatabusUpper = not_14_out ? Condition : 4'bz;  // Controlled_Buffer controlled_buffer_5
  not not_14 (not_14_out, osb);
  and and_7 (CLK, s_r_ff_1_qn, CLKIN);
  Register u_PrimaryBuffer (
    .D({controlled_buffer_3_out, Databus[3:0]}), .en(not_15_out), .clk(CLK), .Q({Instruction, Condition}));  // open: clr
  not not_15 (not_15_out, ipb);
  // Probe on SecondaryBuffer_q
  OctalDTypeLatchOE u_SecondaryBuffer (
    .D0(Databus[0]), .D1(Databus[1]), .D2(Databus[2]), .D3(Databus[3]), .D4(Databus[4]), .D5(Databus[5]),
    .D6(Databus[6]), .CK(nand_1_out), .nOE(osb), .D7(Databus[7]), .Q0(Databus[0]), .Q1(Databus[1]),
    .Q2(Databus[2]), .Q3(Databus[3]), .Q4(Databus[4]), .Q5(Databus[5]), .Q6(Databus[6]), .Q7(Databus[7]),
    .Q(SecondaryBuffer_q));
  nand nand_1 (nand_1_out, CLK, not_17_out);
  assign {DatabusUpper, Databus} = not_16_out ? Address : 12'bz;  // Controlled_Buffer controlled_buffer_6
  not not_16 (not_16_out, opc);
  not not_17 (not_17_out, isb);
  Adder adder_1 (.a(Accumulator), .b(Databus), .out(adder_1_out), .cin(ConditionalFlag), .cout(Carry));
  _74283 #(.ShowInternalStructure("true")) u_74283_1 ();  // open: pin1, pin2, pin3, pin4, pin5, pin6, pin7, pin15, pin14, pin13, pin12, pin11, pin10, pin9
  not not_18 (not_18_out, RESET_t);
  or or_2 (or_2_out, not_18_out, nxt);
  not not_19 (not_19_out, Instruction[3]);
  not not_20 (not_20_out, Condition[0]);
  and and_8 (and_8_out, not_19_out, Condition[0], Instruction[0]);
  and and_9 (and_9_out, not_19_out, not_20_out, Instruction[0]);
  assign nand_2_out = ~(Accumulator & Databus);  // NAND_Gate nand_2, 8 bits wide
  assign {ALUD7, ALUD6, ALUD5, ALUD4, ALUD3, ALUD2, ALUD1, ALUD0} = and_8_out ? {ConditionalFlag, Accumulator[7:1]} : 8'bz;  // Controlled_Buffer controlled_buffer_7
  _74161 #(.ShowInternalStructure("true")) u_74161_4 (
    .pin1(n74161_4_pin1), .pin2(n74161_4_pin2), .pin7(n74161_4_pin7), .pin14(InstructionCounter[0]),
    .pin13(InstructionCounter[1]), .pin12(InstructionCounter[2]), .pin11(InstructionCounter[3]),
    .pin10(n74161_4_pin10), .pin9(n74161_4_pin9));  // open: pin3, pin4, pin5, pin6, pin15
  not not_21 (n74161_4_pin1, or_2_out);
  not not_22 (n74161_4_pin2, CLK);
  and and_10 (and_10_out, Instruction[3], Instruction[0]);
  assign {ALUD7, ALUD6, ALUD5, ALUD4, ALUD3, ALUD2, ALUD1, ALUD0} = and_10_out ? nand_2_out : 8'bz;  // Controlled_Buffer controlled_buffer_8
  assign {ALUD7, ALUD6, ALUD5, ALUD4, ALUD3, ALUD2, ALUD1, ALUD0} = and_9_out ? {Accumulator[6:0], ConditionalFlag} : 8'bz;  // Controlled_Buffer controlled_buffer_9
  not not_23 (not_23_out, Instruction[0]);
  assign {ALUD7, ALUD6, ALUD5, ALUD4, ALUD3, ALUD2, ALUD1, ALUD0} = not_23_out ? adder_1_out : 8'bz;  // Controlled_Buffer controlled_buffer_10
  ROM rom_1 (.addr({Instruction, InstructionCounter}), .data({nxt, rom_1_data[6:4], special, rom_1_data[2:0]}));
  // Probe on Accumulator_q
  OctalDTypeLatchOE u_Accumulator (
    .D0(Databus[0]), .D1(Databus[1]), .D2(Databus[2]), .D3(Databus[3]), .D4(Databus[4]), .D5(Databus[5]),
    .D6(Databus[6]), .CK(nand_3_out), .nOE(1'b0), .D7(Databus[7]), .Q0(Accumulator[0]), .Q1(Accumulator[1]),
    .Q2(Accumulator[2]), .Q3(Accumulator[3]), .Q4(Accumulator[4]), .Q5(Accumulator[5]), .Q6(Accumulator[6]),
    .Q7(Accumulator[7]), .Q(Accumulator_q));
  // Probe on ALUBuffer_q
  OctalDTypeLatchOE ALUBuffer (
    .D0(ALUD0), .D1(ALUD1), .D2(ALUD2), .D3(ALUD3), .D4(ALUD4), .D5(ALUD5), .D6(ALUD6), .CK(nand_4_out),
    .nOE(oalu), .D7(ALUD7), .Q0(Databus[0]), .Q1(Databus[1]), .Q2(Databus[2]), .Q3(Databus[3]),
    .Q4(Databus[4]), .Q5(Databus[5]), .Q6(Databus[6]), .Q7(Databus[7]), .Q(ALUBuffer_q));
  nand nand_3 (nand_3_out, CLK, not_24_out);
  not not_24 (not_24_out, ia);
  nand nand_4 (nand_4_out, CLK, not_25_out);
  not not_25 (not_25_out, ialu);
  assign controlled_buffer_11_out = not_26_out ? Carry : 1'bz;  // Controlled_Buffer controlled_buffer_11
  not not_26 (not_26_out, ucf);
  assign controlled_buffer_11_out = ucf ? ConditionalResult : 1'bz;  // Controlled_Buffer controlled_buffer_12
  _74138 #(.ShowInternalStructure("true")) u_74138_1 (
    .pin1(rom_1_data[0]), .pin2(rom_1_data[1]), .pin3(rom_1_data[2]), .pin4(n74138_1_pin4),
    .pin5(n74138_1_pin5), .pin6(n74138_1_pin6), .pin7(ipcs), .pin15(inone), .pin14(im), .pin13(ipb),
    .pin12(isb), .pin11(ia), .pin10(ialu), .pin9(ipc));
  _74138 #(.ShowInternalStructure("true")) u_74138_2 (
    .pin1(rom_1_data[4]), .pin2(rom_1_data[5]), .pin3(rom_1_data[6]), .pin4(n74138_2_pin4),
    .pin5(n74138_2_pin5), .pin6(n74138_2_pin6), .pin7(opcs), .pin15(onone), .pin14(om), .pin13(opb),
    .pin12(osb), .pin11(oa), .pin10(oalu), .pin9(opc));
  assign Databus = not_27_out ? Accumulator : 8'bz;  // Controlled_Buffer controlled_buffer_13
  not not_27 (not_27_out, oa);
  not not_28 (not_28_out, ialu);
  Register #(.width(1)) register_1 (
    .D(controlled_buffer_11_out), .en(not_28_out), .clk(CLK), .Q(ConditionalFlag));  // open: clr
  not not_29 (not_29_out, ialu);
  and and_11 (ucf, not_29_out, special);
  assign not_30_out = ~Accumulator;  // NOT_Gate not_30, 8 bits wide
  Pull_Resistor #(.pull(1)) pull_resistor_2 (.node(pull_resistor_2_node));
  Adder adder_2 (.a(Databus), .b(not_30_out), .out(adder_2_out), .cin(pull_resistor_2_node), .cout(adder_2_cout));
  _74138 #(.ShowInternalStructure("true")) u_74138_3 (
    .pin1(Condition[1]), .pin2(Condition[2]), .pin3(Condition[3]), .pin4(n74138_3_pin4),
    .pin5(n74138_3_pin5), .pin6(n74138_3_pin6), .pin7(n74138_3_pin7), .pin15(n74138_3_pin15),
    .pin14(n74138_3_pin14), .pin13(n74138_3_pin13), .pin12(n74138_3_pin12), .pin11(n74138_3_pin11),
    .pin10(n74138_3_pin10), .pin9(n74138_3_pin9));
  nor nor_1 (nor_1_out, adder_2_out[0], adder_2_out[1], adder_2_out[2], adder_2_out[3], adder_2_out[4], adder_2_out[5], adder_2_out[6], adder_2_out[7]);
  not not_31 (not_31_out, nor_1_out);
  not not_32 (not_32_out, n74138_3_pin15);
  Pull_Resistor pull_resistor_3 (.node(pull_resistor_3_node));
  assign controlled_buffer_14_out = not_32_out ? pull_resistor_3_node : 1'bz;  // Controlled_Buffer controlled_buffer_14
  not not_33 (not_33_out, n74138_3_pin14);
  assign controlled_buffer_15_out = not_33_out ? Equal : 1'bz;  // Controlled_Buffer controlled_buffer_15
  not not_34 (not_34_out, n74138_3_pin13);
  assign controlled_buffer_16_out = not_34_out ? LessThan : 1'bz;  // Controlled_Buffer controlled_buffer_16
  and and_12 (Equal, nor_1_out, adder_2_cout);
  and and_13 (LessThan, adder_2_cout, not_31_out);
  nor nor_2 (GreaterThan, Equal, LessThan);
  not not_35 (not_35_out, n74138_3_pin12);
  assign controlled_buffer_17_out = not_35_out ? GreaterThan : 1'bz;  // Controlled_Buffer controlled_buffer_17
  not not_36 (not_36_out, n74138_3_pin11);
  assign controlled_buffer_18_out = not_36_out ? D0 : 1'bz;  // Controlled_Buffer controlled_buffer_18
  not not_37 (not_37_out, n74138_3_pin10);
  assign controlled_buffer_19_out = not_37_out ? D1 : 1'bz;  // Controlled_Buffer controlled_buffer_19
  not not_38 (not_38_out, n74138_3_pin9);
  assign controlled_buffer_20_out = not_38_out ? D2 : 1'bz;  // Controlled_Buffer controlled_buffer_20
  Pull_Resistor pull_resistor_4 (.node(controlled_buffer_14_out));
  Pull_Resistor pull_resistor_5 (.node(controlled_buffer_15_out));
  Pull_Resistor pull_resistor_6 (.node(controlled_buffer_16_out));
  Pull_Resistor pull_resistor_7 (.node(controlled_buffer_17_out));
  Pull_Resistor pull_resistor_8 (.node(controlled_buffer_18_out));
  Pull_Resistor pull_resistor_9 (.node(controlled_buffer_19_out));
  Pull_Resistor pull_resistor_10 (.node(controlled_buffer_20_out));
  not not_39 (not_39_out, n74138_3_pin7);
  Pull_Resistor pull_resistor_11 (.node(pull_resistor_11_node));
  assign pull_resistor_11_node = not_39_out ? D3 : 1'bz;  // Controlled_Buffer controlled_buffer_21
  or or_3 (or_3_out, controlled_buffer_14_out, controlled_buffer_15_out, controlled_buffer_16_out, controlled_buffer_17_out, controlled_buffer_18_out, controlled_buffer_19_out, controlled_buffer_20_out, pull_resistor_11_node);
  and and_14 (and_14_out, ucf, Condition[0]);
  not not_40 (not_40_out, or_3_out);
  assign ConditionalResult = and_14_out ? not_40_out : 1'bz;  // Controlled_Buffer controlled_buffer_22
  assign ConditionalResult = and_15_out ? or_3_out : 1'bz;  // Controlled_Buffer controlled_buffer_23
  and and_15 (and_15_out, ucf, not_41_out);
  Pull_Resistor pull_resistor_12 (.node(ConditionalResult));
  not not_41 (not_41_out, Condition[0]);
  // also tied to GND on the sheet: {n74138_1_pin4, n74138_1_pin5, n74138_2_pin4, n74138_2_pin5, n74138_3_pin4, n74138_3_pin5}
  // also tied to VCC on the sheet: {n74161_1_pin7, n74161_1_pin10, n74161_2_pin10, n74161_3_pin10, n74161_4_pin7, n74161_4_pin10, n74161_4_pin9, n74138_1_pin6, n74138_2_pin6, n74138_3_pin6}

  // Other names for the same wires on the sheet: DB0 = Databus[0]; Memory[7:0] = Databus; DB1 = Databus[1];
  //   DB2 = Databus[2]; DB3 = Databus[3]; DB4 = Databus[4]; DB5 = Databus[5]; DB6 = Databus[6]; DB7 = Databus[7];
  //   AQ1 = Accumulator[1]; AQ2 = Accumulator[2]; AQ3 = Accumulator[3]; AQ4 = Accumulator[4]; AQ5 = Accumulator[5];
  //   AQ6 = Accumulator[6]; AQ7 = Accumulator[7]; AQ0 = Accumulator[0];
  //   ALUin[7:0] = {ALUD7, ALUD6, ALUD5, ALUD4, ALUD3, ALUD2, ALUD1, ALUD0}; Dev0 = D0; Dev1 = D1; Dev2 = D2;
  //   Dev3 = D3; HALT = HLT

  // Notes on the sheet:
  //   SL
  //   SR
  //   contents of rom_1 (hex, n*v repeats v):
  //   12 e 14 e 80 11*0 12 e 80 13*0 12 e 13 e 35 54 80 9*0 12 e 5 54 80 11*0 12 e 1d e 80 11*0 12 e 80
  //   13*0 12 e 13 36 80 11*0 12 e 13 e 36 80 10*0 12 e 13 e 67 36 14 76 80 7*0 12 e 13 e 67 36 41 76 80
  //   7*0 12 e 13 e 67 36 13 35 54 76 80 5*0 12 e 13 e 13 35 54 80 8*0 12 5d e 80 12*0 12 e 13 e 67 36 79
  //   e 71 76 80 5*0 12 e 13 36 1a e 13 36 80 7*0 12 e 13 36 1a e 13 36 80
  //   This is basically a Multiplexer
endmodule

module OctalDTypeLatchOE (
  input  D0,
  input  D1,
  input  D2,
  input  D3,
  input  D4,
  input  D5,
  input  D6,
  input  D7,
  input  CK,
  input  nOE,
  output [7:0] Q,
  output Q0,
  output Q1,
  output Q2,
  output Q3,
  output Q4,
  output Q5,
  output Q6,
  output Q7
);

  wire d_ff_1_qn, d_ff_2_qn, d_ff_3_qn, d_ff_4_qn, d_ff_5_qn, d_ff_6_qn, d_ff_7_qn, d_ff_8_qn, not_1_out,
       not_2_out, not_3_out;

  D_Flip_Flop d_ff_1 (.D(D0), .clk(not_2_out), .Q(Q[0]), .Qn(d_ff_1_qn));  // open: preset, reset
  not not_1 (not_1_out, CK);
  not not_2 (not_2_out, not_1_out);
  not not_3 (not_3_out, nOE);
  D_Flip_Flop d_ff_2 (.D(D1), .clk(not_2_out), .Q(Q[1]), .Qn(d_ff_2_qn));  // open: preset, reset
  assign Q0 = not_3_out ? ~d_ff_1_qn : 1'bz;  // Controlled_Inverter controlled_inverter_1
  D_Flip_Flop d_ff_3 (.D(D2), .clk(not_2_out), .Q(Q[2]), .Qn(d_ff_3_qn));  // open: preset, reset
  assign Q1 = not_3_out ? ~d_ff_2_qn : 1'bz;  // Controlled_Inverter controlled_inverter_2
  D_Flip_Flop d_ff_4 (.D(D3), .clk(not_2_out), .Q(Q[3]), .Qn(d_ff_4_qn));  // open: preset, reset
  assign Q2 = not_3_out ? ~d_ff_3_qn : 1'bz;  // Controlled_Inverter controlled_inverter_3
  D_Flip_Flop d_ff_5 (.D(D4), .clk(not_2_out), .Q(Q[4]), .Qn(d_ff_5_qn));  // open: preset, reset
  assign Q3 = not_3_out ? ~d_ff_4_qn : 1'bz;  // Controlled_Inverter controlled_inverter_4
  D_Flip_Flop d_ff_6 (.D(D5), .clk(not_2_out), .Q(Q[5]), .Qn(d_ff_6_qn));  // open: preset, reset
  assign Q4 = not_3_out ? ~d_ff_5_qn : 1'bz;  // Controlled_Inverter controlled_inverter_5
  D_Flip_Flop d_ff_7 (.D(D6), .clk(not_2_out), .Q(Q[6]), .Qn(d_ff_7_qn));  // open: preset, reset
  assign Q5 = not_3_out ? ~d_ff_6_qn : 1'bz;  // Controlled_Inverter controlled_inverter_6
  D_Flip_Flop d_ff_8 (.D(D7), .clk(not_2_out), .Q(Q[7]), .Qn(d_ff_8_qn));  // open: preset, reset
  assign Q6 = not_3_out ? ~d_ff_7_qn : 1'bz;  // Controlled_Inverter controlled_inverter_7
  assign Q7 = not_3_out ? ~d_ff_8_qn : 1'bz;  // Controlled_Inverter controlled_inverter_8
endmodule

module extTest (
);

  main main_1 ();  // open: in_1, D0, RESET, D1, HLT, D2, RES, D3, Address
endmodule
